// Digital circuit ALU 8 BIT.dig as structural Verilog
module ALU_8_BIT (
  input  [3:0] ALUop,
  input  [7:0] A,
  input  [7:0] B,
  input  [2:0] SHAMT,
  output [7:0] S,
  output [7:0] HIGH,
  output ZERO
);

  wire comparator_1_gt;
  wire [1:0] lookuptable_1_out;
  wire [3:0] bitextender_1_out;
  wire [7:0] add_1_s, and_1_out, DIVS_q, DIVU_q, mul_1_mul, multiplexer_1_out, nor_1_out, or_1_out, SLL_out,
       SRA_out, SRL_out, sub_1_s, T0, T1, T2, xor_1_out;

  BitExtender #(.inputBits(3), .outputBits(4)) bitextender_1 (.in(SHAMT), .out(bitextender_1_out));
  Add #(.Bits(8)) add_1 (.a(A), .b(B), .c_i(1'b0), .s(add_1_s));  // open: c_o
  Sub #(.Bits(8)) sub_1 (.a(A), .b(B), .c_i(1'b0), .s(sub_1_s));  // open: c_o
  Mul #(.Bits(8)) mul_1 (.a(A), .b(B), .mul({T0, mul_1_mul}));
  Div #(.Signed("true"), .Bits(8)) DIVS (.a(A), .b(B), .q(DIVS_q), .r(T1));
  Div #(.Bits(8)) DIVU (.a(A), .b(B), .q(DIVU_q), .r(T2));
  assign and_1_out = A & B;  // And and_1, 8 bits wide
  assign or_1_out = A | B;  // Or or_1, 8 bits wide
  assign nor_1_out = ~(A | B);  // NOr nor_1, 8 bits wide
  assign xor_1_out = A ^ B;  // XOr xor_1, 8 bits wide
  BarrelShifter #(.Bits(8)) SLL (.in(B), .shift(bitextender_1_out), .out(SLL_out));
  BarrelShifter #(.Bits(8), .direction("right")) SRL (.in(B), .shift(bitextender_1_out), .out(SRL_out));
  BarrelShifter #(.Bits(8), .barrelShifterMode("arithmetic"), .direction("right")) SRA (
    .in(B), .shift(bitextender_1_out), .out(SRA_out));
  Comparator #(.Bits(8)) comparator_1 (.a(B), .b(A), .gt(comparator_1_gt));  // open: eq, lt
  Multiplexer #(.Bits(8)) multiplexer_1 (.sel(comparator_1_gt), .in_0({8{1'b0}}), .in_1(8'h1), .out(multiplexer_1_out));
  Multiplexer #(.Selector_Bits(4), .Bits(8)) multiplexer_2 (
    .sel(ALUop), .in_0(add_1_s), .in_1(sub_1_s), .in_2({8{1'b0}}), .in_3({8{1'b0}}), .in_4(mul_1_mul),
    .in_5(DIVS_q), .in_6(DIVU_q), .in_7(and_1_out), .in_8(or_1_out), .in_9(nor_1_out), .in_10(xor_1_out),
    .in_11(SLL_out), .in_12(SRL_out), .in_13(SRA_out), .in_14(multiplexer_1_out), .in_15({8{1'b0}}), .out(S));
  Comparator #(.Bits(8)) u_ZERO (.a({8{1'b0}}), .b(S), .eq(ZERO));  // open: gt, lt
  Multiplexer #(.Selector_Bits(2), .Bits(8)) multiplexer_3 (
    .sel(lookuptable_1_out), .in_0({8{1'b0}}), .in_1(T0), .in_2(T1), .in_3(T2), .out(HIGH));
  LookUpTable #(.Bits(2)) lookuptable_1 (
    .in0(ALUop[0]), .in1(ALUop[1]), .in2(ALUop[2]), .in3(ALUop[3]), .out(lookuptable_1_out));

  // Notes on the sheet:
  //   contents of lookuptable_1 (hex, n*v repeats v):
  //   4*0,1,2,3
endmodule
