// Digital circuit CPU.dig as structural Verilog
module CPU (
  input  CLK,
  output [7:0] HI,
  output [7:0] LO
);

  wire alu_8_bit_1_zero, AluSrc, and_1_out, and_2_out, and_3_out, and_4_out, BNE_eq, Branch, JAL, JR_eq,
       Jump, LUI, MemRead, MemtoReg, MemWrite, MFHI_eq, MFLO_eq, nand_1_out, op0, or_1_out, RegDst, RegWrite,
       WRITELOHI;
  wire [1:0] SLIHO;
  wire [2:0] FUNCT, Instruction_Memory_d_2, Instruction_Memory_d_3, multiplexer_2_out, multiplexer_3_out;
  wire [3:0] AluOp, OPCODE;
  wire [5:3] Instruction_Memory_d;
  wire [7:0] add_1_s, add_2_s, add_3_s, alu_8_bit_1_high, alu_8_bit_1_s, barrelshifter_1_out,
       barrelshifter_2_out, bitextender_1_out, DA, Data_Memory_d, multiplexer_1_out, multiplexer_4_out,
       multiplexer_5_out, multiplexer_6_out, multiplexer_7_out, multiplexer_9_out, multiplexer_10_out,
       multiplexer_11_out, PC, Registers_db;

  Add #(.Bits(8)) add_1 (.a(8'h1), .b(PC), .c_i(1'b0), .s(add_1_s));  // open: c_o
  Register #(.Bits(8), .isProgramCounter("true")) u_PC (.D(multiplexer_1_out), .C(CLK), .en(CLK), .Q(PC));
  ROM #(.AddrBits(8), .isProgramMemory("true"), .Bits(16)) Instruction_Memory (
    .A(PC), .sel(1'b1),
    .D({OPCODE, Instruction_Memory_d_3, Instruction_Memory_d_2, Instruction_Memory_d, FUNCT}));
  Multiplexer #(.Bits(8)) multiplexer_1 (.sel(and_2_out), .in_0(multiplexer_5_out), .in_1(DA), .out(multiplexer_1_out));
  Comparator #(.Bits(4)) ZERO (.a(OPCODE), .b(4'b0000), .eq(op0));  // open: gt, lt
  Comparator #(.Bits(4)) u_LUI (.a(OPCODE), .b(4'b1101), .eq(LUI));  // open: gt, lt
  Comparator #(.Bits(4)) u_JAL (.a(OPCODE), .b(4'b0100), .eq(JAL));  // open: gt, lt
  LookUpTable #(.Bits(13)) CONTROLLER (
    .in0(FUNCT[0]), .in1(FUNCT[1]), .in2(FUNCT[2]), .in3(OPCODE[0]), .in4(OPCODE[1]), .in5(OPCODE[2]),
    .in6(OPCODE[3]),
    .out({WRITELOHI, MemRead, AluOp, Jump, Branch, MemWrite, RegWrite, MemtoReg, AluSrc, RegDst}));
  Multiplexer #(.Bits(3)) multiplexer_2 (
    .sel(RegDst), .in_0(Instruction_Memory_d), .in_1(Instruction_Memory_d_2), .out(multiplexer_2_out));
  BitExtender #(.inputBits(6), .outputBits(8)) bitextender_1 (
    .in({Instruction_Memory_d, FUNCT}), .out(bitextender_1_out));
  BarrelShifter #(.Bits(8)) barrelshifter_1 (.in(bitextender_1_out), .shift(4'b0010), .out(barrelshifter_1_out));
  Add #(.Bits(8)) add_2 (.a(add_1_s), .b(barrelshifter_1_out), .c_i(1'b0), .s(add_2_s));  // open: c_o
  Multiplexer #(.Bits(3)) multiplexer_3 (.sel(JAL), .in_0(multiplexer_2_out), .in_1(3'b111), .out(multiplexer_3_out));
  BarrelShifter #(.Bits(8)) barrelshifter_2 (.in(bitextender_1_out), .shift(4'b0100), .out(barrelshifter_2_out));
  Multiplexer #(.Bits(8)) multiplexer_4 (.sel(and_1_out), .in_0(add_1_s), .in_1(add_2_s), .out(multiplexer_4_out));
  Multiplexer #(.Bits(8)) multiplexer_5 (
    .sel(Jump), .in_0(multiplexer_4_out), .in_1({Instruction_Memory_d_2[1:0], Instruction_Memory_d, FUNCT}),
    .out(multiplexer_5_out));
  RegisterFile #(.AddrBits(3), .Bits(8)) Registers (
    .Din(multiplexer_9_out), .we(RegWrite), .Rw(multiplexer_3_out), .C(CLK), .Ra(Instruction_Memory_d_3),
    .Rb(Instruction_Memory_d_2), .Da(DA), .Db(Registers_db));
  Multiplexer #(.Bits(8)) multiplexer_6 (
    .sel(LUI), .in_0(bitextender_1_out), .in_1(barrelshifter_2_out), .out(multiplexer_6_out));
  and and_1 (and_1_out, nand_1_out, Branch);
  nand nand_1 (nand_1_out, BNE_eq, alu_8_bit_1_zero);
  Multiplexer #(.Bits(8)) multiplexer_7 (
    .sel(AluSrc), .in_0(Registers_db), .in_1(multiplexer_6_out), .out(multiplexer_7_out));
  Comparator #(.Bits(3)) MFHI (.a(3'b101), .b(FUNCT), .eq(MFHI_eq));  // open: gt, lt
  Comparator #(.Bits(3)) MFLO (.a(3'b110), .b(FUNCT), .eq(MFLO_eq));  // open: gt, lt
  and and_2 (and_2_out, JR_eq, op0);
  Comparator #(.Bits(4)) BNE (.a(OPCODE), .b(4'b0110), .eq(BNE_eq));  // open: gt, lt
  or or_1 (or_1_out, MFHI_eq, MFLO_eq);
  Comparator #(.Bits(3)) JR (.a(3'b100), .b(FUNCT), .eq(JR_eq));  // open: gt, lt
  and and_3 (and_3_out, or_1_out, op0);
  ALU_8_BIT alu_8_bit_1 (
    .ALUop(AluOp), .S(alu_8_bit_1_s), .A(DA), .B(multiplexer_7_out), .SHAMT(Instruction_Memory_d_3),
    .HIGH(alu_8_bit_1_high), .ZERO(alu_8_bit_1_zero));
  Multiplexer #(.Bits(2)) multiplexer_8 (.sel(and_3_out), .in_0(FUNCT[2:1]), .in_1(2'b00), .out(SLIHO));
  and and_4 (and_4_out, 1'b1, WRITELOHI);
  Register #(.Bits(8)) u_LO (.D(alu_8_bit_1_s), .C(CLK), .en(and_4_out), .Q(LO));
  Register #(.Bits(8)) u_HI (.D(alu_8_bit_1_high), .C(CLK), .en(and_4_out), .Q(HI));
  Multiplexer #(.Selector_Bits(2), .Bits(8)) multiplexer_9 (
    .sel(SLIHO), .in_0(multiplexer_10_out), .in_1(multiplexer_10_out), .in_2(HI), .in_3(LO),
    .out(multiplexer_9_out));
  RAMDualPort #(.AddrBits(8), .Bits(8)) Data_Memory (
    .A(alu_8_bit_1_s), .Din(Registers_db), .str(MemWrite), .C(CLK), .ld(MemRead), .D(Data_Memory_d));
  Multiplexer #(.Bits(8)) multiplexer_10 (
    .sel(JAL), .in_0(multiplexer_11_out), .in_1(add_3_s), .out(multiplexer_10_out));
  Multiplexer #(.Bits(8)) multiplexer_11 (
    .sel(MemtoReg), .in_0(alu_8_bit_1_s), .in_1(Data_Memory_d), .out(multiplexer_11_out));
  Add #(.Bits(8)) add_3 (.a(PC), .b(8'h2), .c_i(1'b0), .s(add_3_s));  // open: c_o

  // Other names for the same wires on the sheet: C = CLK

  // Notes on the sheet:
  //   contents of Instruction_Memory (hex, n*v repeats v):
  //   0,7045
  //   ADDR
  //   OPCODE
  //   8 bits of Address
  //   IMM
  //   RT
  //   RS
  //   FUNCT
  //   RD
  //   contents of CONTROLLER (hex, n*v repeats v):
  //   0,589,609,689,0,4*8,88,88,388,408,1200,1200,1280,1300,488,708
  //   ,208,508,0,0,0,16*40,16*a0,16*b,16*70b,8*38b,16*40b,8*80f,8*12
  //   RegDst
endmodule
